# Fritzing sketch coldroom (saved by Fritzing 0.7.10b)
breadboards: 2

parts:
  Boarduino1 = Boarduino DC v3
  LCD1 = LCD screen
  R1 = Trimmer Potentiometer [maximum_resistance=10kΩ package=THT]
  Part1 = Real Time Clock Module - DS1307 RTC Breakout Board
  S1 = Pushbutton [package="[THT]"]
  RE1 = Rotary Encoder [package=THT]
  J1 = Piezo Speaker
  R2 = Resistor [tolerance=±5% resistance=10k package=THT]
  R3 = Resistor [tolerance=±5% resistance=10k package=THT]

nets:
  GND: Boarduino1.GND, LCD1.VSS, LCD1.R/W, LCD1.LED-, R1.leg2, Part1.GND, J1.pin1, R2.Pin_1, R3.Pin_1
  N1: Boarduino1.D2, S1.Pin_1, S1.Pin_2, R2.Pin_0
  N2: Boarduino1.D5, R3.Pin_0
  N3: Boarduino1.D6, J1.pin2
  N4: Boarduino1.D7, LCD1.RS
  N5: Boarduino1.D8, LCD1.E
  N6: Boarduino1.D9, LCD1.DB3, LCD1.DB4
  N7: Boarduino1.D10, LCD1.DB5
  N8: Boarduino1.D11, LCD1.DB6
  N9: Boarduino1.D12, LCD1.DB7
  N10: Boarduino1.A5, Part1.SCL
  N11: Boarduino1.A4, Part1.SDA
  N12: Boarduino1.A1, RE1.EncoderPinA
  N13: Boarduino1.A0, RE1.EncoderPinB
  +5V: Boarduino1.+5V, LCD1.VDD, LCD1.LED+, R1.leg1, Part1.5V, S1.Pin_3, S1.Pin_4
  N14: LCD1.V0, R1.wiper
